# Fritzing sketch MPU6050_Connections (saved by Fritzing 0.9.3b)
breadboards: 1

parts:
  U1 = NodeMCU V1.0
  GY2 = MPU-6050 Board GY-521 [form="♀ (female)" package=THT]
  R1 = Resistor [tolerance=±5% resistance=220 package="2010 [SMD]"]
  LED1 = LED - 3mm [color="Red (633nm)" package="3 mm [THT]"]

nets:
  N1: U1.D1, GY2.pin3
  N2: U1.D2, GY2.pin4
  N3: U1.GND, GY2.pin2, LED1.cathode
  N4: U1.D5, R1.Pin_1
  N5: U1.3V3, GY2.pin1
  N6: R1.Pin_0, LED1.anode

custom parts:
  NodeMCU V1.0: ESP8266 based NodeMCU
  MPU-6050 Board GY-521: Acelerometro y Giroscopio MPU-6050 Board GY-521
